// Logisim project Banco_Registradores.circ as structural Verilog: 1 circuit, main circuit main
module main (
  input  Reset,
  input  Clock,
  input  [15:0] Data,
  input  [3:0] Wsel,
  input  WriteEnable,
  input  [7:0] D_in,
  input  Dwe,
  input  DF_in,
  input  DFwe,
  input  [3:0] P_in,
  input  Pwe,
  input  [3:0] X_in,
  input  Xwe,
  input  [1:0] PXN_sel,
  input  [3:0] N_in,
  input  Nwe,
  input  [3:0] I_in,
  input  Iwe,
  input  [7:0] T_in,
  input  Twe,
  input  IE_in,
  input  IEwe,
  input  Q_in,
  input  Qwe,
  output [15:0] Data_out,
  output [7:0] D_out,
  output Q_out,
  output [7:0] T_out,
  output DF_out,
  output IE_out,
  output [3:0] I_out
);

  wire R0we, R1we, R2we, R3we, R4we, R5we, R6we, R7we, R8we, R9we, R10we, R11we, R12we, R13we, R14we, R15we;
  wire [3:0] N_q, P_q, Rsel, X_q;
  wire [15:0] R0o, R1o, R2o, R3o, R4o, R5o, R6o, R7o, R8o, R9o, R10o, R11o, R12o, R13o, R14o, R15o;

  Register #(.width(16)) R0 (.D(Data), .en(R0we), .clk(Clock), .Q(R0o), .clr(Reset));
  Register #(.width(16)) R4 (.D(Data), .en(R4we), .clk(Clock), .Q(R4o), .clr(Reset));
  Register #(.width(16)) R8 (.D(Data), .en(R8we), .clk(Clock), .Q(R8o), .clr(Reset));
  Register #(.width(16)) R12 (.D(Data), .en(R12we), .clk(Clock), .Q(R12o), .clr(Reset));
  Register D (.D(D_in), .en(Dwe), .clk(Clock), .Q(D_out), .clr(Reset));
  Register #(.width(1)) DF (.D(DF_in), .en(DFwe), .clk(Clock), .Q(DF_out), .clr(Reset));
  Register #(.width(16)) R1 (.D(Data), .en(R1we), .clk(Clock), .Q(R1o), .clr(Reset));
  Register #(.width(16)) R5 (.D(Data), .en(R5we), .clk(Clock), .Q(R5o), .clr(Reset));
  Register #(.width(16)) R9 (.D(Data), .en(R9we), .clk(Clock), .Q(R9o), .clr(Reset));
  Register #(.width(16)) R13 (.D(Data), .en(R13we), .clk(Clock), .Q(R13o), .clr(Reset));
  Register #(.width(4)) P (.D(P_in), .en(Pwe), .clk(Clock), .Q(P_q), .clr(Reset));
  Register #(.width(4)) X (.D(X_in), .en(Xwe), .clk(Clock), .Q(X_q), .clr(Reset));
  Register #(.width(4)) N (.D(N_in), .en(Nwe), .clk(Clock), .Q(N_q), .clr(Reset));
  Multiplexer #(.select(2), .width(4)) multiplexer_1 (
    .in0(P_q), .in1(X_q), .in2(N_q), .in3(4'b0000), .out(Rsel), .sel(PXN_sel));
  Register #(.width(16)) R2 (.D(Data), .en(R2we), .clk(Clock), .Q(R2o), .clr(Reset));
  Register #(.width(16)) R6 (.D(Data), .en(R6we), .clk(Clock), .Q(R6o), .clr(Reset));
  Register #(.width(16)) R10 (.D(Data), .en(R10we), .clk(Clock), .Q(R10o), .clr(Reset));
  Register #(.width(16)) R14 (.D(Data), .en(R14we), .clk(Clock), .Q(R14o), .clr(Reset));
  Register T (.D(T_in), .en(Twe), .clk(Clock), .Q(T_out), .clr(Reset));
  Register #(.width(4)) I (.D(I_in), .en(Iwe), .clk(Clock), .Q(I_out), .clr(Reset));
  Register #(.width(16)) R3 (.D(Data), .en(R3we), .clk(Clock), .Q(R3o), .clr(Reset));
  Register #(.width(16)) R7 (.D(Data), .en(R7we), .clk(Clock), .Q(R7o), .clr(Reset));
  Register #(.width(16)) R11 (.D(Data), .en(R11we), .clk(Clock), .Q(R11o), .clr(Reset));
  Register #(.width(16)) R15 (.D(Data), .en(R15we), .clk(Clock), .Q(R15o), .clr(Reset));
  Register #(.width(1)) Q (.D(Q_in), .en(Qwe), .clk(Clock), .Q(Q_out), .clr(Reset));
  Register #(.width(1)) IE (.D(IE_in), .en(IEwe), .clk(Clock), .Q(IE_out), .clr(Reset));
  Decoder #(.select(4)) decoder_1 (
    .out0(R0we), .out1(R1we), .out2(R2we), .out3(R3we), .out4(R4we), .out5(R5we), .out6(R6we), .out7(R7we),
    .out8(R8we), .out9(R9we), .out10(R10we), .out11(R11we), .out12(R12we), .out13(R13we), .out14(R14we),
    .out15(R15we), .sel(Wsel), .en(WriteEnable));
  Multiplexer #(.select(4), .width(16)) multiplexer_2 (
    .in0(R0o), .in1(R1o), .in2(R2o), .in3(R3o), .in4(R4o), .in5(R5o), .in6(R6o), .in7(R7o), .in8(R8o),
    .in9(R9o), .in10(R10o), .in11(R11o), .in12(R12o), .in13(R13o), .in14(R14o), .in15(R15o), .out(Data_out),
    .sel(Rsel));

  // Other names for the same wires on the sheet: Rsel_source[1:0] = PXN_sel
endmodule
