// Logisim project arithmetic_logic_unit.circ as structural Verilog: 4 circuits, main circuit ALU
module ALU (
  input  [7:0] Bus_In,
  input  [7:0] D,
  input  Data_Flag,
  input  [2:0] Alu_Op,
  input  Shifter_Direction,
  output [7:0] Alu_Out,
  output Flag_Out
);

  wire adder_1_cout, left_shift_carry_1_carry_out, multiplexer_2_out, right_shift_carry_1_carry_out,
       subtractor_1_bout;
  wire [7:0] adder_1_out, and_1_out, left_shift_carry_1_s, multiplexer_1_out, or_1_out,
       right_shift_carry_1_s, subtractor_1_out, switcher_1_s_a, switcher_1_s_b, xor_1_out;

  assign or_1_out = Bus_In | D;  // OR_Gate or_1, 8 bits wide
  assign and_1_out = Bus_In & D;  // AND_Gate and_1, 8 bits wide
  assign xor_1_out = Bus_In ^ D;  // XOR_Gate xor_1, 8 bits wide
  Adder adder_1 (.a(Bus_In), .b(D), .out(adder_1_out), .cin(Data_Flag), .cout(adder_1_cout));
  Subtractor subtractor_1 (
    .a(switcher_1_s_a), .b(switcher_1_s_b), .out(subtractor_1_out), .bin(Data_Flag), .bout(subtractor_1_bout));
  switcher switcher_1 (.I(Alu_Op[0]), .A(Bus_In), .B(D), .S_A(switcher_1_s_a), .S_B(switcher_1_s_b));
  right_shift_carry right_shift_carry_1 (
    .Carry_In(Data_Flag), .A(Bus_In), .S(right_shift_carry_1_s), .Carry_Out(right_shift_carry_1_carry_out));
  left_shift_carry left_shift_carry_1 (
    .Carry_In(Data_Flag), .A(Bus_In), .S(left_shift_carry_1_s), .Carry_Out(left_shift_carry_1_carry_out));
  Multiplexer #(.width(8)) multiplexer_1 (
    .in0(right_shift_carry_1_s), .in1(left_shift_carry_1_s), .out(multiplexer_1_out), .sel(Shifter_Direction));
  Multiplexer multiplexer_2 (
    .in0(right_shift_carry_1_carry_out), .in1(left_shift_carry_1_carry_out), .out(multiplexer_2_out),
    .sel(Shifter_Direction));
  Multiplexer #(.select(3), .width(8)) multiplexer_3 (
    .in0(Bus_In), .in1(or_1_out), .in2(and_1_out), .in3(xor_1_out), .in4(adder_1_out),
    .in5(subtractor_1_out), .in6(multiplexer_1_out), .in7(subtractor_1_out), .out(Alu_Out), .sel(Alu_Op));
  Multiplexer #(.select(3)) multiplexer_4 (
    .in0(1'b0), .in1(1'b0), .in2(1'b0), .in3(1'b0), .in4(adder_1_cout), .in5(subtractor_1_bout),
    .in6(multiplexer_2_out), .in7(subtractor_1_bout), .out(Flag_Out), .sel(Alu_Op));
endmodule

module left_shift_carry (
  input  Carry_In,
  input  [7:0] A,
  output [7:0] S,
  output Carry_Out
);


  assign Carry_Out = A[7];
  assign S = {A[6:0], Carry_In};
endmodule

module right_shift_carry (
  input  [7:0] A,
  input  Carry_In,
  output Carry_Out,
  output [7:0] S
);


  assign Carry_Out = A[0];
  assign S = {Carry_In, A[7:1]};
endmodule

module switcher (
  input  [7:0] A,
  input  [7:0] B,
  input  I,
  output [7:0] S_A,
  output [7:0] S_B
);

  wire not_1_out, not_2_out;

  not not_1 (not_1_out, I);
  not not_2 (not_2_out, I);
  assign S_B = I ? A : 8'bz;  // Controlled_Buffer controlled_buffer_1
  assign S_A = not_1_out ? A : 8'bz;  // Controlled_Buffer controlled_buffer_2
  assign S_A = I ? B : 8'bz;  // Controlled_Buffer controlled_buffer_3
  assign S_B = not_2_out ? B : 8'bz;  // Controlled_Buffer controlled_buffer_4
endmodule
