// Logisim project memoria_io.circ as structural Verilog: 4 circuits, main circuit addr_latch
// MA
module addr_latch (
  input  [7:0] MA,
  input  TPA,
  input  CLK,
  input  TPB,
  output [7:0] ADDR_HIGH,
  output [15:0] ADDR_FULL,
  output [7:0] ADDR_LOW
);

  Register REG_HIGH (.D(MA), .en(TPA), .clk(CLK), .Q(ADDR_FULL[15:8]));  // open: clr
  Register REG_LOW (.D(MA), .en(TPB), .clk(CLK), .Q(ADDR_FULL[7:0]));  // open: clr

  assign ADDR_HIGH = ADDR_FULL[15:8];
  assign ADDR_LOW = ADDR_FULL[7:0];
endmodule

module memoria_io (
  input  [15:0] R0,
  input  DMA_IN,
  input  DMA_OUT,
  input  [7:0] MA,
  input  TPA,
  input  MWR,
  input  TPB,
  input  MRD,
  input  [7:0] D_IN,
  input  EF1_IN,
  input  EF2_IN,
  input  EF3_IN,
  input  EF4_IN,
  input  Q_REG,
  output R0_INC,
  output DMA_ACK,
  output [7:0] D_OUT,
  output EF1,
  output EF2,
  output EF3,
  output EF4,
  output Q_OUT
);

  wire clock_1_out, dma_ctrl_1_dma_mwr, or_1_out;
  wire [15:0] addr_latch_1_addr_full, dma_ctrl_1_addr_out_15_0;

  addr_latch addr_latch_1 (
    .MA(MA), .TPA(TPA), .CLK(clock_1_out), .TPB(TPB), .ADDR_FULL(addr_latch_1_addr_full));  // open: ADDR_HIGH, ADDR_LOW
  io_ef_q io_ef_q_1 (
    .EF1_IN(EF1_IN), .EF2_IN(EF2_IN), .EF3_IN(EF3_IN), .EF4_IN(EF4_IN), .Q_REG(Q_REG), .EF1(EF1), .EF2(EF2),
    .EF3(EF3), .EF4(EF4), .Q_OUT(Q_OUT));
  dma_ctrl dma_ctrl_1 (
    .CPU_ADDR_15_0(addr_latch_1_addr_full), .R0_15_0(R0), .DMA_IN(DMA_IN), .DMA_OUT(DMA_OUT),
    .ADDR_OUT_15_0(dma_ctrl_1_addr_out_15_0), .DMA_MWR(dma_ctrl_1_dma_mwr), .R0_INC(R0_INC), .DMA_ACK(DMA_ACK));  // open: DMA_DATA_IN_7_0
  Clock clock_1 (.out(clock_1_out));
  RAM #(.addrWidth(16)) ram_1 (
    .addr(dma_ctrl_1_addr_out_15_0), .we(or_1_out), .oe(MRD), .clk(clock_1_out), .din(D_IN), .dout(D_OUT));
  or or_1 (or_1_out, MWR, dma_ctrl_1_dma_mwr);
endmodule

module dma_ctrl (
  input  [7:0] DMA_DATA_IN_7_0,
  input  [15:0] CPU_ADDR_15_0,
  input  [15:0] R0_15_0,
  input  DMA_IN,
  input  DMA_OUT,
  output [15:0] ADDR_OUT_15_0,
  output DMA_MWR,
  output R0_INC,
  output DMA_ACK
);

  Multiplexer #(.width(16)) multiplexer_1 (.in0(CPU_ADDR_15_0), .in1(R0_15_0), .out(ADDR_OUT_15_0), .sel(DMA_ACK));
  or or_1 (DMA_ACK, DMA_IN, DMA_OUT);

  assign DMA_MWR = DMA_IN;
  assign R0_INC = DMA_ACK;
endmodule

module io_ef_q (
  input  EF1_IN,
  input  EF2_IN,
  input  EF3_IN,
  input  EF4_IN,
  input  Q_REG,
  output EF1,
  output EF2,
  output EF3,
  output EF4,
  output Q_OUT
);


  assign EF1 = EF1_IN;
  assign EF2 = EF2_IN;
  assign EF3 = EF3_IN;
  assign EF4 = EF4_IN;
  assign Q_OUT = Q_REG;
endmodule
