// Logisim project pla_decodificador.circ as structural Verilog: 1 circuit, main circuit PLA_decoder
module PLA_decoder (
  input  [7:0] OPCODE,
  output [5:0] INSTR_CLASS,
  output [3:0] N,
  output [3:0] I
);

  ROM #(.dataWidth(6)) DECODER (.addr(OPCODE), .data(INSTR_CLASS));

  assign I = OPCODE[7:4];
  assign N = OPCODE[3:0];

  // Notes on the sheet:
  //   contents of DECODER (hex, n*v repeats v):
  //   0 15*1 16*2 16*3 16*4 16*5 16*6 7 7*8 0 7*9 a b c d e f 10 11 12 13 14 15 16 17 18 19 16*1a 16*1b
  //   16*1c 16*1d 16*1e 16*1f 16*20 21 22 23 24 25 26 27 28 29 2a 2b 2c 2d 2e 2f 30
endmodule
