// Logisim project rca.circ as structural Verilog: 1 circuit, main circuit main
module main (
  input  in_1,
  input  in_2
);

  wire alu_1_flag_out, banco_1_ie_out, banco_1_q_out, clock_1_out, controle_1_p6, controle_1_p7,
       controle_1_p8, controle_1_p9, controle_1_p10, controle_1_p11, decoder_1_out1, decoder_1_out3,
       decoder_1_out4, decoder_1_out5, decoder_1_out6, decoder_1_out7, decoder_1_out8, decoder_1_out9,
       decoder_1_out10, or_1_out;
  wire [1:0] controle_1_p13;
  wire [2:2] controle_1_p13_2;
  wire [3:0] controle_1_p12, controle_1_p14, controle_1_p15;
  wire [5:0] controle_1_p1;
  wire [7:0] alu_1_alu_out, banco_1_d_out, memoria_io_1_d_out;
  wire [15:0] banco_1_data_out, bit_extender_1_out;

  Decoder #(.enable("false"), .select(4)) decoder_1 (
    .out1(decoder_1_out1), .out3(decoder_1_out3), .out4(decoder_1_out4), .out5(decoder_1_out5),
    .out6(decoder_1_out6), .out7(decoder_1_out7), .out8(decoder_1_out8), .out9(decoder_1_out9),
    .out10(decoder_1_out10), .sel(controle_1_p14));  // open: out0, out2, out11, out12, out13, out14, out15
  or or_1 (or_1_out, decoder_1_out3, decoder_1_out4, decoder_1_out5, decoder_1_out6);
  assign bit_extender_1_out = {{8{1'b0}}, memoria_io_1_d_out};  // Bit_Extender bit_extender_1
  Clock clock_1 (.out(clock_1_out));
  Banco banco_1 (
    .Reset(in_2), .Clock(clock_1_out), .Data(bit_extender_1_out), .Wsel(controle_1_p12),
    .WriteEnable(or_1_out), .D_in(alu_1_alu_out), .Dwe(decoder_1_out1), .DF_in(alu_1_flag_out),
    .DFwe(controle_1_p8), .Pwe(decoder_1_out7), .Xwe(decoder_1_out8), .Rsel_source(controle_1_p13),
    .Nwe(controle_1_p9), .Iwe(controle_1_p9), .Twe(decoder_1_out9), .IEwe(decoder_1_out10),
    .Qwe(controle_1_p7), .Data_out(banco_1_data_out), .D_out(banco_1_d_out), .Q_out(banco_1_q_out),
    .IE_out(banco_1_ie_out));  // open: P_in, X_in, N_in, I_in, T_in, IE_in, Q_in, T_out, DF_out, I_out
  // controle controle_1: pin names not known; wires that end beside it: controle_1_p1, clock_1_out, in_2, banco_1_ie_out, banco_1_q_out, controle_1_p6, controle_1_p7, controle_1_p8, controle_1_p9, controle_1_p10, controle_1_p11, controle_1_p12, {controle_1_p13_2[2], controle_1_p13}, controle_1_p14, controle_1_p15
  Comparator comparator_1 (.a({8{1'b0}}), .b(banco_1_d_out), .eq(controle_1_p6));  // open: gt, lt
  ALU alu_1 (
    .Bus_In(memoria_io_1_d_out), .D(banco_1_d_out), .Alu_Op(controle_1_p15[2:0]), .Alu_Out(alu_1_alu_out),
    .Flag_Out(alu_1_flag_out));  // open: Data_Flag, Shifter_Direction
  PLA_decoder pla_decoder_1 (.OPCODE(memoria_io_1_d_out), .INSTR_CLASS(controle_1_p1));  // open: N, I
  memoria_io memoria_io_1 (
    .DMA_IN(in_1), .MA(banco_1_data_out), .MWR(controle_1_p10), .MRD(controle_1_p11), .D_IN(alu_1_alu_out),
    .D_OUT(memoria_io_1_d_out));  // open: R0, DMA_OUT, TPA, TPB, EF1_IN, EF2_IN, EF3_IN, EF4_IN, Q_REG, R0_INC, DMA_ACK, EF1, EF2, EF3, EF4, Q_OUT
endmodule
